// Digital circuit RegisterFile_ALU.dig as structural Verilog
module RegisterFile_ALU (
  input  clk,
  input  [7:0] ctrl_registers,
  input  [1:0] Select_write,
  input  [3:0] Write_data,
  input  [1:0] Select_read1,
  input  [1:0] Select_read2,
  input  [2:0] S1_S0_C_in,
  output [3:0] Output,
  output Overflow
);

  wire register_file_1_p7, register_file_1_p8;

  // Register_File register_file_1: pin names not known; wires that end beside it: Select_read1, Select_read2, clk, Write_data, Select_write, ctrl_registers, register_file_1_p7, register_file_1_p8
  // Arithmetic_Unit arithmetic_unit_1: pin names not known; wires that end beside it: register_file_1_p7, register_file_1_p8, S1_S0_C_in, Output, Overflow
endmodule
